# Fritzing sketch Robot Arm (saved by Fritzing 0.9.2b)
circuit board: 6.88566cm x 5.36311cm
breadboards: 1

parts:
  Servo_A = Basic Servo [part_number=A]
  JACK1 = 2.1mm Barrel Jack with Terminal Block
  Bauteil1 = Arduino Nano (Rev3.0) (ICSP)
  Servo_B = Basic Servo [part_number=B]
  Servo_C = Basic Servo [part_number=C]
  Servo_D = Basic Servo [part_number=D]
  Servo_E = Basic Servo [part_number=E]
  U1 = Voltage Regulator - 6V [package="TO220 [THT]"]

nets:
  GND: Servo_A.gnd, JACK1.NEG, Bauteil1.GND, Servo_B.gnd, Servo_C.gnd, Servo_D.gnd, Servo_E.gnd, U1.GND
  6V: Servo_A.vcc, Servo_B.vcc, Servo_C.vcc, Servo_D.vcc, Servo_E.vcc, U1.output_voltage
  N1: Servo_A.pulse, Bauteil1.D2
  N2: JACK1.POS, U1.input_voltage
  N3: Bauteil1.D3, Servo_B.pulse
  N4: Bauteil1.D4, Servo_C.pulse
  N5: Bauteil1.D5, Servo_D.pulse
  N6: Bauteil1.D6, Servo_E.pulse

notes:
  orange
  red
  brown
  SERVO
  6V VOLTAGE REGULATOR
  12V DC INPUT

custom parts:
  Voltage Regulator - 6V: 6V DC Voltage Regulator

// code stored in the sketch: robotic_arm.ino
#include <Servo.h>
// declare servos
Servo A;
Servo B;
Servo C;
Servo D;
Servo E;

// setup the array of servo positions
int nextServo = 0;
int servoAngles[] = {0,0,0,0,0};

void setup() {
 Serial.begin(115200);
 
 // attach servos to their pins
 A.attach(2);
 B.attach(3);
 C.attach(4);
 D.attach(5);
 E.attach(6);
}

void loop() {
 if(Serial.available()){
	int servoAngle = Serial.read();
	servoAngles[nextServo] = servoAngle;
	nextServo++;
	if(nextServo > 4) nextServo = 0;
 
 
 A.write(servoAngles[0]);
 B.write(servoAngles[1]);
 C.write(servoAngles[2]);
 D.write(servoAngles[3]);
 E.write(servoAngles[4]);
 }

}

// code stored in the sketch: Servo.ino
/*
  Servo
  a potentiometer controls the position of a servo
  
  This example is part of the Fritzing Creator Kit: www.fritzing.org/creator-kit.
*/

#include <Servo.h>                   // include the library Servo.h
 
Servo myservo;                       // creates a servo object
int potpin = 0 ;                     // potentiometer pin declaration
int val;                             // val stores the position of the potentiometer
 
void setup() 
{ 
  myservo.attach(9);                  // connects a servo object to pin 9
} 
 
void loop() 
{ 
  val = analogRead(potpin);            // potentiometer value is read out
  val = map(val, 0, 1023, 0, 179);     // and mapped to the range 0 to 179
  myservo.write(val);                  // turning the servo to the angle in val
  delay(15);                           // give the servo time to react
}
